# Fritzing sketch test001 (saved by Fritzing 0.9.3b)
circuit board: 8.46667cm x 5.64444cm
breadboards: 1

parts:
  LED2 = LED - 5mm [color="Red (633nm)" package="5 mm [THT]"]
  R1 = Resistor [tolerance=±5% resistance=220 package=THT]
  R2 = Resistor [tolerance=±5% resistance=220 package=THT]
  C2 = Ceramic Capacitor [capacitance=100nF package="100 mil [THT, multilayer]"]
  R3 = Textile Analog Pressure Sensor [part_number=PW073]
  C3 = Ceramic Capacitor [capacitance=100nF package="100 mil [THT, multilayer]"]
  R4 = Textile Analog Pressure Sensor [part_number=PW073]
  LED1 = LED - 5mm [color="Red (633nm)" package="5 mm [THT]"]
  Part1 = Arduino Uno (Rev3)

nets:
  GND: LED2.cathode, C2.0, C3.0, LED1.cathode, Part1.GND
  N1: LED2.anode, Part1.D9_PWM
  N2: R1.Pin_0, Part1.D3_PWM
  N3: R1.Pin_1, C2.1, R3.pin_1, Part1.D2
  N4: R2.Pin_0, Part1.D7
  N5: R2.Pin_1, C3.1, R4.pin_1, Part1.D6_PWM
  N6: LED1.anode, Part1.D10_PWM/SS
  5V: Part1.5V

// code stored in the sketch: test001.ino
#include <CapacitiveSensor.h>

CapacitiveSensor cap6_4 = CapacitiveSensor(3, 2);
CapacitiveSensor cap12_10 = CapacitiveSensor(7, 6);
int LED_Y = 9, LED_G = 10, BUZZER = 11;

void setup() {
  pinMode(LED_Y,OUTPUT);
  pinMode(LED_G,OUTPUT);
  pinMode(BUZZER,OUTPUT);
  Serial.begin(9600);
}

void loop() {
  long total1 =  cap6_4.capacitiveSensor(30);
  long total2 =  cap12_10.capacitiveSensor(30);
  total1 = map(total1, 200, 220000, 0, 255);
  total2 = map(total2, 200, 60000, 0, 255);
  
  analogWrite(LED_Y, total1);
  analogWrite(LED_G, total2);
  analogWrite(BUZZER, (total1 + total2)/2);

  Serial.print(total1);
  Serial.print("\t");
  Serial.println(total2);
  delay(10);
}

// code stored in the sketch: test001_fzz.ino
#include <CapacitiveSensor.h>

CapacitiveSensor cap6_4 = CapacitiveSensor(3, 2);
CapacitiveSensor cap12_10 = CapacitiveSensor(7, 6);
int LED_Y = 9, LED_G = 10, BUZZER = 11;

void setup() {
  pinMode(LED_Y,OUTPUT);
  pinMode(LED_G,OUTPUT);
  pinMode(BUZZER,OUTPUT);
  Serial.begin(9600);
}

void loop() {
  long total1 =  cap6_4.capacitiveSensor(30);
  long total2 =  cap12_10.capacitiveSensor(30);
  total1 = map(total1, 200, 220000, 0, 255);
  total2 = map(total2, 200, 60000, 0, 255);
  
  analogWrite(LED_Y, total1);
  analogWrite(LED_G, total2);
  analogWrite(BUZZER, (total1 + total2)/2);

  Serial.print(total1);
  Serial.print("\t");
  Serial.println(total2);
  delay(10);
}
